// Logisim project lab1.circ as structural Verilog: 1 circuit, main circuit main
module main (
  input  X1,
  input  X2,
  input  X2_2,
  output Y
);

  wire and_1_out, not_1_out;

  and and_1 (and_1_out, X1, X2, X2_2);
  not not_1 (not_1_out, and_1_out);
  or or_1 (Y, X1, not_1_out);
endmodule
