// Logisim project lab2.circ as structural Verilog: 1 circuit, main circuit main
module main (
  input  x3,
  input  x2,
  input  x1,
  input  x0,
  input  x3_2,
  input  x2_2,
  input  x1_2,
  input  x0_2,
  output out_9,
  output out_10
);

  wire and_1_out, and_2_out, and_3_out, and_4_out, and_5_out, and_6_out, and_7_out, and_8_out, not_1_out,
       not_2_out, not_3_out, not_4_out, not_5_out, not_6_out, not_7_out, not_8_out, not_9_out, not_10_out,
       not_11_out, not_12_out, not_13_out, not_14_out, not_15_out, not_16_out;

  not not_1 (not_1_out, x3);
  not not_2 (not_2_out, x2);
  not not_3 (not_3_out, x0);
  not not_4 (not_4_out, x3);
  not not_5 (not_5_out, x1);
  not not_6 (not_6_out, x0);
  not not_7 (not_7_out, x3);
  not not_8 (not_8_out, x0);
  not not_9 (not_9_out, x1);
  not not_10 (not_10_out, x0);
  not not_11 (not_11_out, x1);
  and and_1 (and_1_out, not_1_out, not_2_out, x1, not_3_out);
  and and_2 (and_2_out, not_4_out, x2, not_5_out, not_6_out);
  and and_3 (and_3_out, not_7_out, x2, x1, not_8_out);
  and and_4 (and_4_out, x3, x2, not_9_out, not_10_out);
  and and_5 (and_5_out, x3, x2, not_11_out, x0);
  or or_1 (out_9, and_1_out, and_2_out, and_3_out, and_4_out, and_5_out);
  not not_12 (not_12_out, x1_2);
  not not_13 (not_13_out, x0_2);
  not not_14 (not_14_out, x1_2);
  not not_15 (not_15_out, x3_2);
  not not_16 (not_16_out, x0_2);
  and and_6 (and_6_out, x2_2, not_12_out, not_13_out);
  and and_7 (and_7_out, x3_2, x2_2, not_14_out);
  and and_8 (and_8_out, not_15_out, x1_2, not_16_out);
  or or_2 (out_10, and_6_out, and_7_out, and_8_out);
endmodule
