// Logisim project lab3.circ as structural Verilog: 1 circuit, main circuit main
module main (
  output x3,
  output x1,
  output x0,
  output out_4,
  output x3_2,
  output x2,
  output x1_2,
  output x0_2,
  output out_9
);

  wire nand_1_out, nand_2_out, nand_3_out, nand_4_out, nor_1_out, nor_2_out, nor_3_out, nor_4_out, nor_5_out,
       nor_6_out, nor_7_out, nor_8_out, nor_9_out;

  nand nand_1 (nand_1_out, x3, x3);
  nand nand_2 (nand_2_out, x1, x1);
  nand nand_3 (nand_3_out, nand_1_out, nand_2_out);
  nand nand_4 (nand_4_out, x0, x0);
  nor nor_1 (nor_1_out, x3_2, x3_2);
  nor nor_2 (nor_2_out, x2, x2);
  nor nor_3 (nor_3_out, x1_2, x1_2);
  nor nor_4 (nor_4_out, x3_2, x3_2);
  nor nor_5 (nor_5_out, x1_2, x1_2);
  nand nand_5 (out_4, nand_3_out, nand_4_out);
  nor nor_6 (nor_6_out, nor_1_out, nor_2_out);
  nor nor_7 (nor_7_out, nor_3_out, x0_2);
  nor nor_8 (nor_8_out, nor_4_out, x2, x0_2);
  nor nor_9 (nor_9_out, nor_5_out, x3_2, x2);
  nor nor_10 (out_9, nor_6_out, nor_7_out, nor_8_out, nor_9_out);
endmodule
